// Logisim project Task3.circ as structural Verilog: 1 circuit, main circuit main
// Q1
module main (
  input  D0,
  input  D1,
  input  D2,
  input  D3,
  input  EN,
  output Q0,
  output Q1,
  output Q2,
  output Q3
);

  wire CLK_out, multiplexer_1_out, multiplexer_2_out, multiplexer_3_out, multiplexer_4_out;

  Clock CLK (.out(CLK_out));
  Multiplexer multiplexer_1 (.in0(Q0), .in1(D0), .out(multiplexer_1_out), .sel(EN));
  Multiplexer multiplexer_2 (.in0(Q1), .in1(D1), .out(multiplexer_2_out), .sel(EN));
  Multiplexer multiplexer_3 (.in0(Q2), .in1(D2), .out(multiplexer_3_out), .sel(EN));
  Multiplexer multiplexer_4 (.in0(Q3), .in1(D3), .out(multiplexer_4_out), .sel(EN));
  D_Flip_Flop d_ff_1 (.D(multiplexer_1_out), .clk(CLK_out), .Q(Q0));  // open: Qn, preset, reset
  D_Flip_Flop d_ff_2 (.D(multiplexer_2_out), .clk(CLK_out), .Q(Q1));  // open: Qn, preset, reset
  D_Flip_Flop d_ff_3 (.D(multiplexer_3_out), .clk(CLK_out), .Q(Q2));  // open: Qn, preset, reset
  D_Flip_Flop d_ff_4 (.D(multiplexer_4_out), .clk(CLK_out), .Q(Q3));  // open: Qn, preset, reset
endmodule
