// Logisim project Task4.circ as structural Verilog: 1 circuit, main circuit main
module main (
  input  in_1
);

  wire and_1_out, and_2_out, clock_1_out, d_ff_1_q, d_ff_2_q, multiplexer_1_out, multiplexer_2_out,
       not_1_out, or_1_out, or_2_out;

  or or_1 (or_1_out, d_ff_2_q, not_1_out);
  not not_1 (not_1_out, d_ff_1_q);
  and and_1 (and_1_out, not_1_out, d_ff_2_q);
  Clock clock_1 (.out(clock_1_out));
  Multiplexer multiplexer_1 (.in0(and_1_out), .in1(or_1_out), .out(multiplexer_1_out), .sel(in_1));
  D_Flip_Flop d_ff_1 (.D(multiplexer_1_out), .clk(clock_1_out), .Q(d_ff_1_q));  // open: Qn, preset, reset
  or or_2 (or_2_out, d_ff_1_q, d_ff_2_q);
  and and_2 (and_2_out, d_ff_2_q, d_ff_1_q);
  Multiplexer multiplexer_2 (.in0(and_2_out), .in1(or_2_out), .out(multiplexer_2_out), .sel(in_1));
  D_Flip_Flop d_ff_2 (.D(multiplexer_2_out), .clk(clock_1_out), .Q(d_ff_2_q));  // open: Qn, preset, reset
endmodule
